# Fritzing sketch Esquema solenoidesX3 (saved by Fritzing 0.9.2b)
breadboards: 1

parts:
  L1 = Solenoid
  L2 = Solenoid
  L3 = Solenoid
  D1 = Diode [package=diode-hv]
  VCC1 = Battery
  KY-1 = Keyes Relay [package=THT]
  D2 = Diode [package=diode-hv]
  D3 = Diode [package=diode-hv]

nets:
  N1: L1.pin1, L2.pin1, L3.pin1, D1.A, VCC1.-, D2.A, D3.A
  N2: L1.pin2, L2.pin2, L3.pin2, D1.C, KY-1.NO, D2.C, D3.C
  N3: VCC1.+, KY-1.C

custom parts:
  Keyes Relay: The Keyes 5V relay module is suitable for SCM development, home appliance control. It uses a 5V~12V TIL control signal which can control DC / AC signal.
