# Fritzing sketch Esquema tira led (saved by Fritzing 0.9.2b)
circuit board: 8.46667cm x 5.64444cm
breadboards: 1

parts:
  U1 = WS2812 RGB LED strip
  U2 = WS2812 RGB LED strip
  U3 = WS2812 RGB LED strip
  U4 = WS2812 RGB LED strip
  U5 = WS2812 RGB LED strip
  R1 = Resistor [tolerance=±5% resistance=470 package="1206 [SMD]"]
  R2 = Resistor [tolerance=±5% resistance=470 package="1206 [SMD]"]
  R3 = Resistor [tolerance=±5% resistance=470 package="1206 [SMD]"]
  R4 = Resistor [tolerance=±5% resistance=470 package="1206 [SMD]"]
  R5 = Resistor [tolerance=±5% resistance=470 package="1206 [SMD]"]
  Part1 = Arduino Mega 2560 (Rev3)
  VCC1 = 4 x AAA Battery Mount

nets:
  GND: U1.GND, U2.GND, U3.GND, U4.GND, U5.GND, Part1.GND, VCC1.-
  VCC: U1.VCC, U2.VCC, U3.VCC, U4.VCC, U5.VCC, VCC1.+
  N1: U1.DIN, R5.Pin_1
  N2: U2.DIN, R1.Pin_1
  N3: U3.DIN, R2.Pin_1
  N4: U4.DIN, R4.Pin_1
  N5: U5.DIN, R3.Pin_1
  N6: R1.Pin_0, Part1.A2
  N7: R2.Pin_0, Part1.A1
  N8: R3.Pin_0, Part1.A0
  N9: R4.Pin_0, Part1.A3
  N10: R5.Pin_0, Part1.A4

custom parts:
  WS2812 RGB LED strip: WS2812 strip
