# Fritzing sketch arduino-rasp-pantalla (saved by Fritzing 0.9.3b)

parts:
  part = Arduino Mega 2560 (Rev3)
  part_2 = Raspberry Pi Pico
  part_3 = TFT 2.8 inch 320x240 Touch w microSD [part_number=SCREN]

nets:
  3V3: part.3V3, part_2.pin_36, part_3.3.3V
  GND: part.GND, part_2.pin_3, part_2.pin_13, part_2.pin_28, part_3.GND
  N1: part_2.pin_19, part_3.LCD_RST
  N2: part_2.pin_20, part_3.LCD_DC
  N3: part_2.pin_21, part_3.MISO
  N4: part_2.pin_22, part_3.LCD_CS
  N5: part_2.pin_24, part_3.SCLK
  N6: part_2.pin_25, part_3.MOSI

custom parts:
  Raspberry Pi Pico: Raspberry Pi Pico. Based around the RP2040 microcontroller the Pico is a low cost microcontroller device bringing Raspberry Pi quality, cost, and easy of use to the microcontroller space. Jan 2021, Split part in to two versions: SMD (this one) and tht. This one is single sided and uses the castellation pads to solder the module to the board (no holes, other than for the USB connector!). The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
  TFT 2.8 inch 320x240 Touch w microSD: This TFT display is big (2.8" diagonal) bright (4 white-LED backlight) and colorful! 240x320 pixels with individual RGB pixel control. As a bonus, this display has a resistive touchscreen attached to it already, so you can detect finger presses anywhere on the screen.
