# Fritzing sketch serial-arduino-rasp-pantalla (saved by Fritzing 0.9.3b)

parts:
  part = Raspberry Pi Pico
  part_2 = Arduino Mega 2560 (Rev3)
  part_3 = 2.8" SPI TFT Module

nets:
  N1: part.pin_5, part_2.D20/SDA, part_2.SDA
  N2: part.pin_6, part_2.D21/SCL, part_2.SCL
  N3: part.pin_8, part.pin_42, part_3.pin2
  N4: part.pin_9, part_3.pin5
  N5: part.pin_10, part_3.pin4
  N6: part.pin_19, part_3.pin7
  N7: part.pin_20, part_3.pin6
  N8: part.pin_22, part_3.pin3
  N9: part.pin_36, part_3.pin1, part_3.pin8

custom parts:
  Raspberry Pi Pico: Raspberry Pi Pico. Based around the RP2040 microcontroller the Pico is a low cost microcontroller device bringing Raspberry Pi quality, cost, and easy of use to the microcontroller space. Jan 2021, Split part in to two versions: tht (this one) and SMD. This one will drill holes for a .1 in header in pcb to allow plugging in the module as well as providing pads to solder the module to the top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
  2.8" SPI TFT Module: A generic 2.8 inch LCD TFT 320x240 display with touchscreen and SD card slot. Uses the ILI9341 controller, like the Adafruit displays of this size uses.
